# Fritzing sketch 7-segment-display layout (saved by Fritzing 0.9.6b)
breadboards: 1

parts:
  Part1 = Arduino Uno (Rev3)
  U1 = 7-SEGMENT-DISPLAY [package=7-segment-display]
  R1 = Resistor [tolerance=±5% power=0.25 resistance=220 package=THT]
  R3 = Resistor [tolerance=±5% power=0.25 resistance=220 package=THT]
  R4 = Resistor [tolerance=±5% power=0.25 resistance=220 package=THT]
  R5 = Resistor [tolerance=±5% power=0.25 resistance=220 package=THT]
  R6 = Resistor [tolerance=±5% power=0.25 resistance=220 package=THT]
  R9 = Resistor [tolerance=±5% power=0.25 resistance=220 package=THT]
  R10 = Resistor [tolerance=±5% power=0.25 resistance=220 package=THT]
  R12 = Resistor [tolerance=±5% power=0.25 resistance=220 package=THT]

nets:
  N1: Part1.D8, R3.Pin_0
  N2: Part1.D9_PWM, R12.Pin_0
  N3: Part1.D2, R1.Pin_0
  N4: Part1.D3_PWM, R9.Pin_0
  N5: Part1.D4, R6.Pin_0
  N6: Part1.D5_PWM, R10.Pin_0
  N7: Part1.D6_PWM, R5.Pin_0
  N8: Part1.D7, R4.Pin_0
  N9: Part1.GND, U1.C, U1.F
  N10: U1.E, R3.Pin_1
  N11: U1.D, R4.Pin_1
  N12: U1.G1, R5.Pin_1
  N13: U1.DP, R10.Pin_1
  N14: U1.B, R6.Pin_1
  N15: U1.A, R9.Pin_1
  N16: U1.G2, R1.Pin_1
  N17: U1.G, R12.Pin_1
