# Fritzing sketch schematic (saved by Fritzing 0.9.6b)
breadboards: 1

parts:
  Part1 = Arduino Uno (Rev3)
  R1 = Resistor [tolerance=±5% power=0.25 resistance=220 package=THT]
  LED1 = LED - 5mm [color="Red (633nm)" current=0.030 package="5 mm [THT]"]
  S1 = Pushbutton [package="[THT]"]
  R2 = Resistor [tolerance=±5% power=0.25 resistance=220 package=THT]

nets:
  N1: Part1.GND, R1.Pin_0, R2.Pin_0
  N2: Part1.D2, LED1.anode
  N3: Part1.D3_PWM, S1.Pin_1, S1.Pin_2, S1.Pin_3, S1.Pin_4, R2.Pin_1
  N4: R1.Pin_1, LED1.cathode
